// Logisim project jrmips.circ as structural Verilog: 8 circuits, main circuit main
module main (
);

  wire alu_1_branch, Clock_out, decoder_alu_enablewrite_1_enablewrite, decoder_everything_else_1_puthalt,
       decoder_everything_else_1_ramaccess, demultiplexer_1_out0, demultiplexer_1_out1, demultiplexer_2_out1,
       not_1_out, not_2_out, Reset_out, split_1_subop;
  wire [1:0] decoder_everything_else_1_aluinamux, decoder_everything_else_1_aluinbmux,
       decoder_everything_else_1_enablewrite2, decoder_everything_else_1_jumpmux;
  wire [2:0] decoder_alu_enablewrite_1_alu, split_1_registera, split_1_registerb;
  wire [3:0] put_1_led0, put_1_led1, put_1_led2, put_1_led3;
  wire [4:0] split_1_opcode;
  wire [7:0] adder_1_out, bit_extender_1_out, multiplexer_1_out, PC_q, register_1_readdata1,
       split_1_immediate;
  wire [15:0] alu_1_result, bit_extender_2_out, bit_extender_3_out, bit_extender_4_out, bit_extender_5_out,
       multiplexer_2_out, multiplexer_3_out, multiplexer_4_out, multiply_divide_1_reg1,
       multiply_divide_1_reg2, ram_1_data, register_1_readdata2, rom_1_data;
  wire [15:8] register_1_readdata1_2;

  Multiplexer #(.select(2), .width(8), .enable("false")) multiplexer_1 (
    .in0(adder_1_out), .in2(split_1_immediate), .in3(register_1_readdata1), .out(multiplexer_1_out),
    .sel(decoder_everything_else_1_jumpmux));  // open: in1
  not not_1 (not_1_out, demultiplexer_1_out0);
  Clock Clock (.out(Clock_out));
  assign bit_extender_1_out = {{7{1'b0}}, 1'b1};  // Bit_Extender bit_extender_1
  Register_part PC (.D(multiplexer_1_out), .en(not_1_out), .Q(PC_q), .clk(Clock_out), .clr(Reset_out));
  Button Reset (.out(Reset_out));
  Adder adder_1 (.a(bit_extender_1_out), .b(PC_q), .out(adder_1_out));  // open: cin, cout
  assign bit_extender_2_out = {{8{1'b0}}, adder_1_out};  // Bit_Extender bit_extender_2
  LED led_1 (.in(demultiplexer_1_out0));
  Hex_Digit_Display hex_digit_display_1 (.value(put_1_led3));  // open: dp
  ROM #(.dataWidth(16)) rom_1 (.addr(PC_q), .data(rom_1_data));  // open: sel
  Hex_Digit_Display hex_digit_display_2 (.value(put_1_led2));  // open: dp
  Demultiplexer #(.enable("false")) demultiplexer_1 (
    .out0(demultiplexer_1_out0), .out1(demultiplexer_1_out1), .in(decoder_everything_else_1_puthalt),
    .sel(not_2_out));
  Decoder_Everything_Else decoder_everything_else_1 (
    .OpCodeAndSubOp(split_1_opcode), .RAMAccess(decoder_everything_else_1_ramaccess),
    .PutHalt(decoder_everything_else_1_puthalt), .ALUInAMUX(decoder_everything_else_1_aluinamux),
    .ALUInBMUX(decoder_everything_else_1_aluinbmux), .JumpMUX(decoder_everything_else_1_jumpmux),
    .EnableWrite2(decoder_everything_else_1_enablewrite2[0]), .Branch(alu_1_branch));
  Decoder_ALU_EnableWrite decoder_alu_enablewrite_1 (
    .OpCodeAndSubOp(split_1_opcode), .ALU(decoder_alu_enablewrite_1_alu),
    .EnableWrite(decoder_alu_enablewrite_1_enablewrite));
  Split split_1 (
    .Instruction(rom_1_data), .Subop(split_1_subop), .Immediate(split_1_immediate),
    .RegisterB(split_1_registerb), .RegisterA(split_1_registera), .Opcode(split_1_opcode));
  assign bit_extender_3_out = {{8{split_1_immediate[7]}}, split_1_immediate};  // Bit_Extender bit_extender_3
  assign bit_extender_4_out = {{8{1'b0}}, split_1_immediate};  // Bit_Extender bit_extender_4
  assign bit_extender_5_out = {{15{1'b0}}, 1'b0};  // Bit_Extender bit_extender_5
  Hex_Digit_Display hex_digit_display_3 (.value(put_1_led1));  // open: dp
  Hex_Digit_Display hex_digit_display_4 (.value(put_1_led0));  // open: dp
  Put put_1 (
    .Print({register_1_readdata1_2, register_1_readdata1}), .LED3(put_1_led3), .LED2(put_1_led2),
    .LED1(put_1_led1), .LED0(put_1_led0), .EnablePut(demultiplexer_1_out1), .Clock(Clock_out),
    .in_4(Reset_out));
  not not_2 (not_2_out, split_1_subop);
  Register register_1 (
    .WriteData1(multiplexer_4_out), .ReadRegister2(split_1_registerb),
    .ReadData1({register_1_readdata1_2, register_1_readdata1}), .ReadData2(register_1_readdata2),
    .EnableWrite(decoder_alu_enablewrite_1_enablewrite), .Clock(Clock_out), .Reset(Reset_out),
    .ReadRegister1(split_1_registera), .EnableWrite2(decoder_everything_else_1_enablewrite2[0]),
    .WriteData2(multiply_divide_1_reg2));
  Multiplexer #(.select(2), .width(16), .enable("false")) multiplexer_2 (
    .in0({register_1_readdata1_2, register_1_readdata1}), .in1(bit_extender_2_out), .in2(bit_extender_5_out),
    .out(multiplexer_2_out), .sel(decoder_everything_else_1_aluinamux));  // open: in3
  Multiplexer #(.select(2), .width(16), .enable("false")) multiplexer_3 (
    .in0(register_1_readdata2), .in1(bit_extender_3_out), .in2(bit_extender_4_out), .in3(bit_extender_5_out),
    .out(multiplexer_3_out), .sel(decoder_everything_else_1_aluinbmux));
  ALU alu_1 (
    .A(multiplexer_2_out), .B(multiplexer_3_out), .Branch(alu_1_branch), .Result(alu_1_result),
    .Opcode(decoder_alu_enablewrite_1_alu), .Subop(split_1_subop));
  Multiply_Divide multiply_divide_1 (
    .A({register_1_readdata1_2, register_1_readdata1}), .B(register_1_readdata2), .Subop(split_1_subop),
    .Reg1(multiply_divide_1_reg1), .Reg2(multiply_divide_1_reg2));
  Demultiplexer #(.enable("false")) demultiplexer_2 (
    .out0(decoder_everything_else_1_enablewrite2[1]), .out1(demultiplexer_2_out1),
    .in(decoder_everything_else_1_ramaccess), .sel(split_1_subop));
  RAM #(.dataWidth(16), .bus("separate")) ram_1 (
    .addr(register_1_readdata2[7:0]), .din({register_1_readdata1_2, register_1_readdata1}),
    .data(ram_1_data), .str(demultiplexer_2_out1), .clk(Clock_out),
    .ld(decoder_everything_else_1_enablewrite2[1]));  // open: sel, clr
  Multiplexer #(.select(2), .width(16), .enable("false")) multiplexer_4 (
    .in0(alu_1_result), .in1(multiply_divide_1_reg1), .in2(ram_1_data), .out(multiplexer_4_out),
    .sel(decoder_everything_else_1_enablewrite2));  // open: in3

  // Notes on the sheet:
  //   Brian Choromanski
  //   BJC76@pitt.edu
  //   JumpMUX
  //   ROM
  //   Instruction Memory
  //   Put/Halt
  //   contents of rom_1 (hex, n*v repeats v):
  //   8000 7200 9032 8202 7240 9032 8404 7280 9032 8606 72c0 9032 8808 7300 9032 8a0a 7340 9032 8c0c 7380
  //   9032 8e0e 73c0 9032 b001 b200 9001
  //   ALUInAMUX
  //   ALUInBMUX
  //   RAMAccess
  //   RAM
  //   Data Memory
  //   StoreMUX
endmodule

module ALU (
  input  [15:0] A,
  input  Subop,
  input  [2:0] Opcode,
  input  [15:0] B,
  output Branch,
  output [15:0] Result
);

  wire comparator_1_eq, comparator_1_gt, comparator_1_lt, not_1_out;
  wire [15:0] adder_1_out, and_1_out, bit_extender_1_out, bit_extender_2_out, bit_extender_3_out,
       bit_extender_4_out, multiplexer_1_out, multiplexer_2_out, multiplexer_3_out, multiplexer_4_out,
       multiplexer_5_out, nor_1_out, shifter_1_out, shifter_2_out, subtractor_1_out;

  assign and_1_out = A & B;  // AND_Gate and_1, 16 bits wide
  Multiplexer #(.width(16), .enable("false")) multiplexer_1 (
    .in0(and_1_out), .in1(nor_1_out), .out(multiplexer_1_out), .sel(Subop));
  assign nor_1_out = ~(A | B);  // NOR_Gate nor_1, 16 bits wide
  Adder #(.width(16)) adder_1 (.a(A), .b(B), .out(adder_1_out));  // open: cin, cout
  Multiplexer #(.width(16), .enable("false")) multiplexer_2 (
    .in0(adder_1_out), .in1(subtractor_1_out), .out(multiplexer_2_out), .sel(Subop));
  Subtractor #(.width(16)) subtractor_1 (.a(A), .b(B), .out(subtractor_1_out));  // open: bin, bout
  Shifter #(.width(16)) shifter_1 (.in(A), .\dist (B[3:0]), .out(shifter_1_out));
  Multiplexer #(.width(16), .enable("false")) multiplexer_3 (
    .in0(shifter_1_out), .in1(shifter_2_out), .out(multiplexer_3_out), .sel(Subop));
  Shifter #(.width(16), .shift("lr")) shifter_2 (.in(A), .\dist (B[3:0]), .out(shifter_2_out));
  not not_1 (not_1_out, comparator_1_eq);
  Comparator #(.width(16)) comparator_1 (
    .a(A), .b(B), .gt(comparator_1_gt), .eq(comparator_1_eq), .lt(comparator_1_lt));
  assign bit_extender_1_out = {{15{1'b0}}, not_1_out};  // Bit_Extender bit_extender_1
  Multiplexer #(.width(16), .enable("false")) multiplexer_4 (
    .in0(bit_extender_1_out), .in1(bit_extender_2_out), .out(multiplexer_4_out), .sel(Subop));
  assign bit_extender_2_out = {{15{1'b0}}, comparator_1_eq};  // Bit_Extender bit_extender_2
  assign bit_extender_3_out = {{15{1'b0}}, comparator_1_gt};  // Bit_Extender bit_extender_3
  Multiplexer #(.width(16), .enable("false")) multiplexer_5 (
    .in0(bit_extender_3_out), .in1(bit_extender_4_out), .out(multiplexer_5_out), .sel(Subop));
  assign bit_extender_4_out = {{15{1'b0}}, comparator_1_lt};  // Bit_Extender bit_extender_4
  Multiplexer #(.select(3), .width(16), .enable("false")) multiplexer_6 (
    .in0(multiplexer_1_out), .in1(adder_1_out), .in2(multiplexer_2_out), .in3(multiplexer_3_out),
    .in4(multiplexer_4_out), .in5(multiplexer_5_out), .in6(multiplexer_5_out), .in7(multiplexer_5_out),
    .out(Result), .sel(Opcode));
  or or_1 (Branch, Result[0], Result[0], Result[1], Result[2], Result[3], Result[4], Result[5], Result[6], Result[7], Result[8], Result[9], Result[10], Result[11], Result[12], Result[13], Result[14], Result[15]);
endmodule

module Register (
  input  EnableWrite,
  input  [2:0] ReadRegister1,
  input  [2:0] ReadRegister2,
  input  [15:0] WriteData1,
  input  EnableWrite2,
  input  Clock,
  input  Reset,
  input  [15:0] WriteData2,
  output [15:0] ReadData1,
  output [15:0] ReadData2
);

  wire demultiplexer_1_out0, demultiplexer_1_out1, demultiplexer_1_out2, demultiplexer_1_out3,
       demultiplexer_1_out4, demultiplexer_1_out5, demultiplexer_1_out6, demultiplexer_1_out7,
       demultiplexer_2_out0, demultiplexer_2_out1, demultiplexer_2_out2, demultiplexer_2_out3,
       demultiplexer_2_out4, demultiplexer_2_out5, demultiplexer_2_out6, demultiplexer_2_out7, or_1_out,
       or_2_out, or_3_out, or_4_out, or_5_out, or_6_out, or_7_out, or_8_out;
  wire [2:0] adder_1_out, bit_extender_1_out;
  wire [15:0] or_9_out, or_10_out, or_11_out, or_12_out, or_13_out, or_14_out, or_15_out, or_16_out, s0, s1,
       s2, s3, s4, s5, s6, s7, Write_s0, Write_s0_2, Write_s1, Write_s1_2, Write_s2, Write_s2_2, Write_s3,
       Write_s3_2, Write_s4, Write_s4_2, Write_s5, Write_s5_2, Write_s6, Write_s6_2, Write_s7, Write_s7_2;

  Demultiplexer #(.select(3), .enable("false")) demultiplexer_1 (
    .out0(demultiplexer_1_out0), .out1(demultiplexer_1_out1), .out2(demultiplexer_1_out2),
    .out3(demultiplexer_1_out3), .out4(demultiplexer_1_out4), .out5(demultiplexer_1_out5),
    .out6(demultiplexer_1_out6), .out7(demultiplexer_1_out7), .in(EnableWrite), .sel(ReadRegister1));
  assign bit_extender_1_out = {{2{1'b0}}, 1'b1};  // Bit_Extender bit_extender_1
  Demultiplexer #(.select(3), .enable("false")) demultiplexer_2 (
    .out0(demultiplexer_2_out0), .out1(demultiplexer_2_out1), .out2(demultiplexer_2_out2),
    .out3(demultiplexer_2_out3), .out4(demultiplexer_2_out4), .out5(demultiplexer_2_out5),
    .out6(demultiplexer_2_out6), .out7(demultiplexer_2_out7), .in(EnableWrite2), .sel(adder_1_out));
  Adder #(.width(3)) adder_1 (.a(ReadRegister1), .b(bit_extender_1_out), .out(adder_1_out));  // open: cin, cout
  or or_1 (or_1_out, demultiplexer_1_out0, demultiplexer_2_out0);
  or or_2 (or_2_out, demultiplexer_1_out1, demultiplexer_2_out1);
  or or_3 (or_3_out, demultiplexer_1_out2, demultiplexer_2_out2);
  or or_4 (or_4_out, demultiplexer_1_out3, demultiplexer_2_out3);
  or or_5 (or_5_out, demultiplexer_1_out4, demultiplexer_2_out4);
  or or_6 (or_6_out, demultiplexer_1_out5, demultiplexer_2_out5);
  or or_7 (or_7_out, demultiplexer_1_out6, demultiplexer_2_out6);
  or or_8 (or_8_out, demultiplexer_1_out7, demultiplexer_2_out7);
  assign or_9_out = Write_s0 | Write_s0_2;  // OR_Gate or_9, 16 bits wide
  Register_part #(.width(16)) u_s0 (.D(or_9_out), .en(or_1_out), .Q(s0), .clk(Clock), .clr(Reset));
  assign or_10_out = Write_s1 | Write_s1_2;  // OR_Gate or_10, 16 bits wide
  Register_part #(.width(16)) u_s1 (.D(or_10_out), .en(or_2_out), .Q(s1), .clk(Clock), .clr(Reset));
  assign or_11_out = Write_s2 | Write_s2_2;  // OR_Gate or_11, 16 bits wide
  Register_part #(.width(16)) u_s2 (.D(or_11_out), .en(or_3_out), .Q(s2), .clk(Clock), .clr(Reset));
  assign or_12_out = Write_s3 | Write_s3_2;  // OR_Gate or_12, 16 bits wide
  Register_part #(.width(16)) u_s3 (.D(or_12_out), .en(or_4_out), .Q(s3), .clk(Clock), .clr(Reset));
  assign or_13_out = Write_s4 | Write_s4_2;  // OR_Gate or_13, 16 bits wide
  Register_part #(.width(16)) u_s4 (.D(or_13_out), .en(or_5_out), .Q(s4), .clk(Clock), .clr(Reset));
  assign or_14_out = Write_s5 | Write_s5_2;  // OR_Gate or_14, 16 bits wide
  Register_part #(.width(16)) u_s5 (.D(or_14_out), .en(or_6_out), .Q(s5), .clk(Clock), .clr(Reset));
  assign or_15_out = Write_s6 | Write_s6_2;  // OR_Gate or_15, 16 bits wide
  Register_part #(.width(16)) u_s6 (.D(or_15_out), .en(or_7_out), .Q(s6), .clk(Clock), .clr(Reset));
  assign or_16_out = Write_s7 | Write_s7_2;  // OR_Gate or_16, 16 bits wide
  Register_part #(.width(16)) u_s7 (.D(or_16_out), .en(or_8_out), .Q(s7), .clk(Clock), .clr(Reset));
  Multiplexer #(.select(3), .width(16), .enable("false")) multiplexer_1 (
    .in0(s0), .in1(s1), .in2(s2), .in3(s3), .in4(s4), .in5(s5), .in6(s6), .in7(s7), .out(ReadData1),
    .sel(ReadRegister1));
  Multiplexer #(.select(3), .width(16), .enable("false")) multiplexer_2 (
    .in0(s0), .in1(s1), .in2(s2), .in3(s3), .in4(s4), .in5(s5), .in6(s6), .in7(s7), .out(ReadData2),
    .sel(ReadRegister2));
  Demultiplexer #(.select(3), .width(16), .enable("false")) demultiplexer_3 (
    .out0(Write_s0), .out1(Write_s1), .out2(Write_s2), .out3(Write_s3), .out4(Write_s4), .out5(Write_s5),
    .out6(Write_s6), .out7(Write_s7), .in(WriteData1), .sel(ReadRegister1));
  Demultiplexer #(.select(3), .width(16), .enable("false")) demultiplexer_4 (
    .out0(Write_s0_2), .out1(Write_s1_2), .out2(Write_s2_2), .out3(Write_s3_2), .out4(Write_s4_2),
    .out5(Write_s5_2), .out6(Write_s6_2), .out7(Write_s7_2), .in(WriteData2), .sel(adder_1_out));
endmodule

module Multiply_Divide (
  input  Subop,
  input  [15:0] A,
  input  [15:0] B,
  output [15:0] Reg1,
  output [15:0] Reg2
);

  wire [15:0] divider_1_out, divider_1_rem, multiplier_1_cout, multiplier_1_out;

  Divider #(.width(16)) divider_1 (.a(A), .b(B), .out(divider_1_out), .rem(divider_1_rem));  // open: upper
  Multiplier #(.width(16)) multiplier_1 (.a(A), .b(B), .out(multiplier_1_out), .cout(multiplier_1_cout));  // open: cin
  Multiplexer #(.width(16), .enable("false")) multiplexer_1 (
    .in0(divider_1_out), .in1(multiplier_1_out), .out(Reg1), .sel(Subop));
  Multiplexer #(.width(16), .enable("false")) multiplexer_2 (
    .in0(divider_1_rem), .in1(multiplier_1_cout), .out(Reg2), .sel(Subop));
endmodule

module Split (
  input  [15:0] Instruction,
  output Subop,
  output [7:0] Immediate,
  output [2:0] RegisterB,
  output [2:0] RegisterA,
  output [4:0] Opcode
);


  assign Immediate = Instruction[8:1];
  assign Opcode = {Instruction[15:12], Instruction[0]};
  assign RegisterA = Instruction[11:9];
  assign RegisterB = Instruction[8:6];
  assign Subop = Instruction[0];
endmodule

module Put (
  input  [15:0] Print,
  input  EnablePut,
  input  Clock,
  input  in_4,
  output [3:0] LED3,
  output [3:0] LED2,
  output [3:0] LED1,
  output [3:0] LED0
);

  Register_part #(.width(16), .trigger("falling")) register_1 (
    .D(Print), .en(EnablePut), .Q({LED3, LED2, LED1, LED0}), .clk(Clock), .clr(in_4));
endmodule

// Decode1
module Decoder_ALU_EnableWrite (
  input  [4:0] OpCodeAndSubOp,
  output [2:0] ALU,
  output EnableWrite
);

  wire and_1_out, and_2_out, and_3_out, and_4_out, and_5_out, and_6_out, and_7_out, and_8_out, and_9_out,
       and_10_out, and_11_out, and_12_out, and_13_out, not_1_out, not_2_out, not_3_out, not_4_out, not_5_out,
       not_6_out, not_7_out, not_8_out, not_9_out, not_10_out, not_11_out, not_12_out, not_13_out,
       not_14_out, not_15_out, not_16_out, not_17_out, not_18_out;

  and and_1 (and_1_out, OpCodeAndSubOp[3], OpCodeAndSubOp[1]);
  and and_2 (and_2_out, OpCodeAndSubOp[3], OpCodeAndSubOp[2]);
  and and_3 (and_3_out, OpCodeAndSubOp[4], OpCodeAndSubOp[1], OpCodeAndSubOp[0]);
  not not_1 (not_1_out, OpCodeAndSubOp[3]);
  not not_2 (not_2_out, OpCodeAndSubOp[2]);
  not not_3 (not_3_out, OpCodeAndSubOp[1]);
  not not_4 (not_4_out, OpCodeAndSubOp[3]);
  not not_5 (not_5_out, OpCodeAndSubOp[1]);
  not not_6 (not_6_out, OpCodeAndSubOp[4]);
  not not_7 (not_7_out, OpCodeAndSubOp[3]);
  not not_8 (not_8_out, OpCodeAndSubOp[4]);
  not not_9 (not_9_out, OpCodeAndSubOp[2]);
  not not_10 (not_10_out, OpCodeAndSubOp[1]);
  not not_11 (not_11_out, OpCodeAndSubOp[3]);
  not not_12 (not_12_out, OpCodeAndSubOp[2]);
  not not_13 (not_13_out, OpCodeAndSubOp[1]);
  not not_14 (not_14_out, OpCodeAndSubOp[3]);
  not not_15 (not_15_out, OpCodeAndSubOp[2]);
  not not_16 (not_16_out, OpCodeAndSubOp[0]);
  not not_17 (not_17_out, OpCodeAndSubOp[4]);
  not not_18 (not_18_out, OpCodeAndSubOp[0]);
  or or_1 (ALU[2], and_1_out, and_2_out, and_3_out);
  and and_4 (and_4_out, not_1_out, OpCodeAndSubOp[2]);
  and and_5 (and_5_out, OpCodeAndSubOp[3], not_2_out, not_3_out);
  and and_6 (and_6_out, OpCodeAndSubOp[4], OpCodeAndSubOp[1], OpCodeAndSubOp[0]);
  and and_7 (and_7_out, not_4_out, OpCodeAndSubOp[1]);
  and and_8 (and_8_out, OpCodeAndSubOp[3], not_5_out);
  and and_9 (and_9_out, not_6_out, not_7_out);
  and and_10 (and_10_out, not_8_out, not_9_out, not_10_out);
  and and_11 (and_11_out, not_11_out, not_12_out, not_13_out);
  and and_12 (and_12_out, not_14_out, not_15_out, not_16_out);
  and and_13 (and_13_out, not_17_out, OpCodeAndSubOp[2], OpCodeAndSubOp[1], not_18_out);
  or or_2 (ALU[1], and_4_out, and_5_out, and_6_out);
  or or_3 (ALU[0], and_7_out, and_8_out, OpCodeAndSubOp[4]);
  or or_4 (EnableWrite, and_9_out, and_10_out, and_11_out, and_12_out, and_13_out);
endmodule

// Decoder 2
module Decoder_Everything_Else (
  input  [4:0] OpCodeAndSubOp,
  input  Branch,
  output RAMAccess,
  output PutHalt,
  output [1:0] ALUInAMUX,
  output [1:0] ALUInBMUX,
  output [1:0] JumpMUX,
  output EnableWrite2
);

  wire and_1_out, and_2_out, and_3_out, and_4_out, and_7_out, and_8_out, and_11_out, and_12_out, and_13_out,
       and_14_out, and_15_out, and_16_out, and_19_out, not_1_out, not_2_out, not_3_out, not_4_out, not_5_out,
       not_6_out, not_7_out, not_8_out, not_9_out, not_10_out, not_11_out, not_12_out, not_13_out,
       not_14_out, not_15_out, not_16_out, not_17_out, or_2_out, or_4_out;

  not not_1 (not_1_out, OpCodeAndSubOp[4]);
  not not_2 (not_2_out, OpCodeAndSubOp[3]);
  not not_3 (not_3_out, OpCodeAndSubOp[4]);
  not not_4 (not_4_out, OpCodeAndSubOp[2]);
  not not_5 (not_5_out, OpCodeAndSubOp[4]);
  not not_6 (not_6_out, OpCodeAndSubOp[1]);
  not not_7 (not_7_out, OpCodeAndSubOp[1]);
  and and_1 (and_1_out, OpCodeAndSubOp[1], OpCodeAndSubOp[0]);
  and and_2 (and_2_out, OpCodeAndSubOp[3], OpCodeAndSubOp[1]);
  and and_3 (and_3_out, OpCodeAndSubOp[3], OpCodeAndSubOp[2]);
  and and_4 (and_4_out, OpCodeAndSubOp[4], OpCodeAndSubOp[1]);
  not not_8 (not_8_out, OpCodeAndSubOp[0]);
  not not_9 (not_9_out, OpCodeAndSubOp[3]);
  not not_10 (not_10_out, OpCodeAndSubOp[2]);
  not not_11 (not_11_out, OpCodeAndSubOp[3]);
  not not_12 (not_12_out, OpCodeAndSubOp[1]);
  not not_13 (not_13_out, OpCodeAndSubOp[0]);
  not not_14 (not_14_out, OpCodeAndSubOp[3]);
  not not_15 (not_15_out, OpCodeAndSubOp[2]);
  not not_16 (not_16_out, OpCodeAndSubOp[4]);
  not not_17 (not_17_out, OpCodeAndSubOp[3]);
  and and_5 (RAMAccess, not_1_out, OpCodeAndSubOp[3], OpCodeAndSubOp[2], OpCodeAndSubOp[1]);
  and and_6 (PutHalt, OpCodeAndSubOp[4], not_2_out, OpCodeAndSubOp[2], OpCodeAndSubOp[1]);
  and and_7 (and_7_out, not_3_out, OpCodeAndSubOp[3], not_4_out, OpCodeAndSubOp[1]);
  and and_8 (and_8_out, not_5_out, OpCodeAndSubOp[3], OpCodeAndSubOp[2], not_6_out);
  and and_9 (ALUInAMUX[0], OpCodeAndSubOp[4], OpCodeAndSubOp[1]);
  and and_10 (ALUInAMUX[1], OpCodeAndSubOp[4], not_7_out);
  or or_1 (ALUInBMUX[1], and_1_out, and_2_out, and_3_out, and_4_out);
  and and_11 (and_11_out, OpCodeAndSubOp[1], not_8_out);
  and and_12 (and_12_out, OpCodeAndSubOp[3], OpCodeAndSubOp[1]);
  and and_13 (and_13_out, OpCodeAndSubOp[3], OpCodeAndSubOp[2]);
  and and_14 (and_14_out, OpCodeAndSubOp[4], OpCodeAndSubOp[0]);
  and and_15 (and_15_out, OpCodeAndSubOp[4], not_9_out, not_10_out, OpCodeAndSubOp[1]);
  and and_16 (and_16_out, OpCodeAndSubOp[4], not_11_out, OpCodeAndSubOp[2], not_12_out, not_13_out);
  and and_17 (JumpMUX[0], OpCodeAndSubOp[4], not_14_out, not_15_out, OpCodeAndSubOp[1], OpCodeAndSubOp[0]);
  and and_18 (EnableWrite2, not_16_out, not_17_out, OpCodeAndSubOp[2], OpCodeAndSubOp[1]);
  or or_2 (or_2_out, and_7_out, and_8_out);
  or or_3 (ALUInBMUX[0], and_11_out, and_12_out, OpCodeAndSubOp[4], and_13_out, and_14_out);
  or or_4 (or_4_out, and_15_out, and_16_out);
  and and_19 (and_19_out, or_2_out, Branch);
  or or_5 (JumpMUX[1], and_19_out, or_4_out);
endmodule
